// Digital circuit soc.dig as structural Verilog
module soc (
  input  clk,
  output [31:0] x1
);

  wire [13:0] u_cpu_pc_2;
  wire [31:0] rom_1_d, u_cpu_pc;

  ROM #(.AddrBits(14), .Bits(32)) rom_1 (.A(u_cpu_pc_2), .sel(1'b1), .D(rom_1_d));
  cpu #(.applicationType("IVERILOG"), .CodeFile("cpu.v")) u_cpu (
    .instr(rom_1_d), .resetn(1'b1), .clk(clk), .PC({u_cpu_pc[31:16], u_cpu_pc_2, u_cpu_pc[1:0]}), .x1(x1));

  // Notes on the sheet:
  //   clk: Hz: 10
  //   contents of rom_1 (hex, n*v repeats v):
  //   100093,100113,193,2081b3,8113,18093,ff5ff06f
endmodule
